# Fritzing sketch IR_communication (saved by Fritzing 0.9.3b)
circuit board: 8.46667cm x 5.64444cm
breadboards: 1

parts:
  IR_Receiver = TSOP312.., 314.. [package=THT]
  Part1 = Arduino Uno (Rev3) - ICSP
  Componente2 = Arduino Uno (Rev3)
  IR_Transmiter = LED - 5mm [color="Infrared (850nm)" package="5 mm [THT]"]
  R1 = Resistor [tolerance=±5% resistance=220 package=THT]
  UART_Receiver = USB connector [package=THT]  # not connected
  UART_Transmiter = USB connector [package=THT]  # not connected

nets (from the breadboard view):
  N1: IR_Receiver.GND, Part1.ICSP_MOSI, Part1.D11_PWM/MOSI
  N2: IR_Receiver.Vs, Part1.AREF, Componente2.GND
  N3: IR_Receiver.Data, Part1.5V
  N4: Part1.D0/RX, Componente2.D1/TX
  N5: Part1.D1/TX, Componente2.D0/RX
  N6: Componente2.D2, R1.Pin_1
  N7: IR_Transmiter.anode, R1.Pin_0

// code stored in the sketch: IR rec decoder.ino
#include <IRremote.h> // By MMKaresz

int RECV_PIN = 11;
int ONE = 2;
int TWO = 3;
int THREE = 4;
int FOUR = 5;
int pwm = 0 ;
int ONEval = 2;
int TWOval = 2;
int THREEval = 2;
int FOURval= 2;
IRrecv irrecv(RECV_PIN);

decode_results results;

void setup() {
  Serial.begin(9600);
  irrecv.enableIRIn(); // Start the receiver
  pinMode(ONE, OUTPUT);
  pinMode(TWO, OUTPUT);
  pinMode(THREE, OUTPUT);
  pinMode(FOUR, OUTPUT);
  digitalWrite(ONE, LOW);
  digitalWrite(TWO, LOW);
  digitalWrite(THREE, LOW);
  analogWrite(FOUR, 0);
}

void loop() {
  if (irrecv.decode(&results)) {
    Serial.println(results.value);  // Shows the IR remote code in the serial monitor
      switch (results.value){

    case 3249166758:          // btn 1
      Serial.print("ONE - "); 
      Serial.println(ONEval);
      ONEval=ONEval+1;			//counts up, switch on if its even number
      if (ONEval % 2) { digitalWrite(ONE,HIGH); }				// if its even number...
      if ( (ONEval & 0x01) == 0) { digitalWrite(ONE,LOW); }		//if its odd number...
      delay(200);
    break;
      
    case 3249147378:          //btn 2
    Serial.print("TWO - ");
    Serial.println(TWOval);
      TWOval=TWOval+1;
      if (TWOval % 2) { digitalWrite(TWO,HIGH); }				// if its even number...
      if ( (TWOval & 0x01) == 0) { digitalWrite(TWO,LOW); }		//if its odd number...
      delay(200);
    break;
   
    case 3249152478:          //btn 3
      Serial.print("THREE - ");
      Serial.println(THREEval);
      THREEval=THREEval+1;
      if (THREEval % 2) { digitalWrite(THREE,HIGH); }       	// if its even number...
      if ( (THREEval & 0x01) == 0) { digitalWrite(THREE,LOW); } //if its odd number...
      delay(200);
      break;

    case 3249180018:         // vol up
      Serial.print("up - ");    
    	pwm=pwm+5;
    	if (pwm>=255){
    		pwm=255;
    	}
    	analogWrite(FOUR,pwm);  
    	Serial.println(pwm);
      break;
    
    case 3249196338:        // vol down
      Serial.print("down - ");    
	   	pwm=pwm-5;
    	if (pwm<=0){
    		pwm=0;
    	}
    	analogWrite(FOUR,pwm);  
      	Serial.println(pwm);
      break;
      
    case 3249195318:       // 1-2-3 off
      Serial.println("OFF");    
      digitalWrite(ONE,LOW);
      digitalWrite(TWO,LOW);
      digitalWrite(THREE,LOW);
      ONEval = 2;
      TWOval = 2;
      THREEval = 2;
      break;
 }
  delay(20);
  if (ONEval==5) { ONEval=1;}
  if (TWOval==5) { TWOval=1;}
  if (THREEval==5) { THREEval=1;}
  irrecv.resume(); // Receive the next value
  }
}
